# Fritzing sketch diagrama (saved by Fritzing 0.9.3b)
circuit board: 8.46667cm x 5.64444cm
breadboards: 1

parts:
  Part1 = RFID-RC522-v3
  R1 = Resistor [tolerance=±5% resistance=220 package=THT]
  R2 = Resistor [tolerance=±5% resistance=220 package=THT]
  LED1 = LED - 5mm [color="Red (633nm)" package="5 mm [THT]"]
  LED2 = LED - 5mm [color="Green (555nm)" package="5 mm [THT]"]
  J1 = Piezo Speaker
  VCC1 = 4 x AAA Battery Mount
  M1 = DOIT Esp32 DevKit v1 (30 pins long, 11 pins width) [part_number=ESP32S-PIN30]
  U2 = RELAY [package=relay-jzc]
  D1 = Rectifier Diode [part_number=1N4001 package="300 mil [THT]"]
  Power_plug1 = Power plug

nets:
  N1: Part1.SDA, M1.D21
  N2: Part1.SCK, M1.D18
  N3: Part1.MOSI, M1.D23
  N4: Part1.MISO, M1.D19
  GND: Part1.GND, R1.Pin_0, R2.Pin_0, J1.pin1, VCC1.-, M1.GND, U2.NO, D1.anode, Power_plug1.GND
  N5: Part1.RST, M1.D22
  3.3V: Part1.3.3V, M1.3V3, U2.COIL2, U2.COIL1, D1.cathode, Power_plug1.VCC
  N6: LED1.cathode, M1.D26
  N7: LED2.cathode, M1.D25
  N8: J1.pin2, M1.D33
  N9: VCC1.+, U2.NC

custom parts:
  RFID-RC522-v3: A simple China made RFID-RC522 Reader (6x4 cm); do check the pin labels, as this is a MFRC522 based clone.
  DOIT Esp32 DevKit v1 (30 pins long, 11 pins width): The DOIT Esp32 DevKit v1 is one of the development board created by DOIT to evaluate the ESP-WROOM-32 module. It is based on the ESP32 microcontroller that boasts Wifi, Bluetooth, Ethernet and Low Power support all in a single chip. (vanepp) made breadboard work, adjusted pin numbering and labels and reduced size of schematic and cleaned up pcb. This chip is 30pins long (2 x15) and 11 pins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

// code stored in the sketch: Untitled2.ino
/*
 * 
 * All the resources for this project: http://randomnerdtutorials.com/
 * Modified by José Vicente
 * 
 * Created by Japtech
 * 
 */
 
#include <SPI.h>
#include <MFRC522.h>
#include <LiquidCrystal.h>
 
#define SS_PIN 53
#define RST_PIN 6
LiquidCrystal lcd(12, 11, 5, 4, 3, 2);

MFRC522 mfrc522(SS_PIN, RST_PIN);   // Create MFRC522 instance.

void setup() 
{
  lcd.begin(16, 2);
  pinMode(7, OUTPUT);
  pinMode(8, OUTPUT);
  Serial.begin(9600);   // Initiate a serial communication
  SPI.begin();      // Initiate  SPI bus
  mfrc522.PCD_Init();   // Initiate MFRC522
  Serial.println("Approximate your card to the reader...");
  Serial.println();
  lcd.print("waiting for card");
}
void loop() 
{
  // Look for new cards
  
  if ( ! mfrc522.PICC_IsNewCardPresent()) 
  {
    return;
  }
  // Select one of the cards
  if ( ! mfrc522.PICC_ReadCardSerial()) 
  {
    return;
  }
  //Show UID on serial monitor
  Serial.print("UID tag :");
  String content= "";
  byte letter;
  for (byte i = 0; i < mfrc522.uid.size; i++) 
  {
     Serial.print(mfrc522.uid.uidByte[i] < 0x10 ? " 0" : " ");
     Serial.print(mfrc522.uid.uidByte[i], HEX);
         
     content.concat(String(mfrc522.uid.uidByte[i] < 0x10 ? " 0" : " "));
     content.concat(String(mfrc522.uid.uidByte[i], HEX));
  }
  Serial.println();
  Serial.print("Message : ");
  content.toUpperCase();
  if (content.substring(1) == "63 8C E5 C7") //change here the UID of the card/cards that you want to give access
  {
    Serial.println("Authorized access");
    lcd.clear();
    lcd.print("Authorized access");
    digitalWrite(7, HIGH);
    delay(3000);
    digitalWrite(7, LOW);
    lcd.clear();
    lcd.print("waiting for card");
    Serial.println();
  }
 
 else   {
    Serial.println(" Access denied");
    lcd.clear();
    lcd.print(" Access denied");
    digitalWrite(8, HIGH);
    delay(3000);
    digitalWrite(8, LOW);
    lcd.clear();
    lcd.print("waiting for card");
  }
}
